# Fritzing sketch PondAutomation (saved by Fritzing 0.9.3b)

parts:
  DS1 = DS18B20 1-Wire Temperature Sensor Probe
  A1 = VL53lox
  DS2 = DS18B20 1-Wire Temperature Sensor Probe
  DS3 = DS18B20 1-Wire Temperature Sensor Probe
  Mod2 = Heltec WiFi Kit 8 [part_number=HTIT-W8266]

nets:
  GND: DS1.GND, A1.Pin_2, DS2.GND, DS3.GND, Mod2.pin_13
  N1: DS1.DQ, DS2.DQ, DS3.DQ, Mod2.pin_18, Mod2.pin_19
  VDD: DS1.VDD, A1.Pin_1, DS2.VDD, DS3.VDD, Mod2.pin_14
  N2: A1.Pin_3, Mod2.pin_6
  N3: A1.Pin_4, Mod2.pin_17, Mod2.pin_20

custom parts:
  VL53lox: VL53L0X Time-of-Flight (ToF) Laser Ranging Sensor Breakout.
  Heltec WiFi Kit 8: The Heltec WiFi Kit 8 is an IoT development board designed and produced by Heltec Automation and based on the Espressif ESP8266 processor module. The board includes built-in WiFi, a 0.91″ OLED display and a Li-Po battery management system. Links: Heltec WiFi Kit 32 product page Github
